# Fritzing sketch attiny85_schematic (saved by Fritzing 0.9.3b)
breadboards: 1

parts:
  SI4735 = IC, DIP package, 24 pins [chip_label=IC]
  L1 = Inductor [package="400 mil [THT]"]
  C3 = Capacitor [part_number=470nF package=cap-pth-large]
  C2 = Capacitor [part_number=1nF package=cap-pth-small2]
  FM_Antenna = Antenna
  C1 = Capacitor [part_number=22nF package=cap-pth-large]
  X1 = CRYSTAL [package=crystal-32khz-smd_epson_mc146]
  R3 = Resistor [tolerance=±5% resistance=2.2k package="0402 [SMD]"]
  R4 = Resistor [tolerance=±5% resistance=3.3k package="0402 [SMD]"]
  R5 = Resistor [tolerance=±5% resistance=3.3k package="0402 [SMD]"]
  C4 = Capacitor [part_number=100nF package=cap-pth-large]
  TO_AMP = Audio Jack (TRS) 3.5mm [package="4Ucon 08780 [THT]"]
  C7 = Capacitor [part_number=4.7uF package=cap-pth-large]
  C8 = Capacitor [part_number=4.7uF package=cap-pth-large]
  C5 = Capacitor [part_number=22pF package=cap-pth-large]
  C6 = Capacitor [part_number=22pF package=cap-pth-large]
  part = attiny85 [package=dip]
  SEEK_UP = SWITCH-MOMENTARY-2 [package=tactile-pth]
  SEEK_DOWN = SWITCH-MOMENTARY-2 [package=tactile-pth]
  I2C_LCD = OLED 128x64  # not connected

nets:
  N1: SI4735.pin3, R3.Pin_1
  N2: SI4735.pin8, C2.2
  N3: SI4735.pin9, L1.pin_1
  GND: SI4735.pin10, SI4735.pin13, SI4735.pin16, C4.1, C5.1, C6.1, part.Pin_4, SEEK_UP.2, SEEK_DOWN.2
  N4: SI4735.pin12, C3.1
  N5: SI4735.pin15, part.Pin_2
  N6: SI4735.pin17, R4.Pin_1, part.Pin_7
  N7: SI4735.pin18, R5.Pin_1, part.Pin_5
  N8: SI4735.pin19, X1.2, C6.2
  3.3V: SI4735.pin20, SI4735.pin21, R4.Pin_0, R5.Pin_0, C4.2, part.Pin_8
  N9: SI4735.pin22, C1.1
  N10: SI4735.pin23, C8.1
  N11: SI4735.pin24, C7.1
  N12: L1.pin_0, C3.2
  N13: C2.1, FM_Antenna.antenna_lead
  N14: X1.1, R3.Pin_0, C5.2
  N15: TO_AMP.Ring, C8.2
  N16: TO_AMP.Tip, C7.2
  N17: part.Pin_3, SEEK_UP.1
  N18: part.Pin_6, SEEK_DOWN.1

notes:
  SI47XX AND ATTINY85
  This circuit uses internal pullup resource
  Ricardo Lima Caratti - JAN 2020
  SCLK / SCL
  SDIO / SDA
  RESET (RST)
  Left Out
  Right Out
  Look for the right display Arduino Library to control your I2C device.
  R4 and R5 may depend on the devices connected to the I2C bus. Try to use the lowest possible value.

custom parts:
  OLED 128x64: Grove OLED 128x64
