# Fritzing sketch basic_schematic (saved by Fritzing 0.9.3b)
breadboards: 1

parts:
  part = Arduino Pro Mini v13
  SI4735 = IC, DIP package, 24 pins [chip_label=IC]
  L1 = Inductor [package="400 mil [THT]"]
  C3 = Capacitor [part_number=470nF package=cap-pth-large]
  C2 = Capacitor [part_number=1nF package=cap-pth-small2]
  FM_Antenna = Antenna
  C1 = Capacitor [part_number=22nF package=cap-pth-large]
  X1 = CRYSTAL [package=crystal-32khz-smd_epson_mc146]
  R3 = Resistor [tolerance=±5% resistance=2.2k package="0402 [SMD]"]
  R4 = Resistor [tolerance=±5% resistance=10k package="0402 [SMD]"]
  R5 = Resistor [tolerance=±5% resistance=10k package="0402 [SMD]"]
  C4 = Capacitor [part_number=100nF package=cap-pth-large]
  TO_AMP = Audio Jack (TRS) 3.5mm [package="4Ucon 08780 [THT]"]
  C7 = Capacitor [part_number=4.7uF package=cap-pth-large]
  C8 = Capacitor [part_number=4.7uF package=cap-pth-large]
  C5 = Capacitor [part_number=22pF package=cap-pth-large]
  C6 = Capacitor [part_number=22pF package=cap-pth-large]

nets:
  N1: part.A4, SI4735.pin18, R4.Pin_1
  N2: part.A5, SI4735.pin17, R5.Pin_0
  GND: part.GND, SI4735.pin10, SI4735.pin13, SI4735.pin16, C4.1, C5.1, C6.1
  3.3V: part.VCC, SI4735.pin20, SI4735.pin21, R4.Pin_0, R5.Pin_1, C4.2
  N3: part.D12/MISO, SI4735.pin15
  N4: part.D2, SI4735.pin4
  N5: SI4735.pin3, R3.Pin_1
  N6: SI4735.pin8, C2.2
  N7: SI4735.pin9, L1.pin_1
  N8: SI4735.pin12, C3.1
  N9: SI4735.pin19, X1.2, C6.2
  N10: SI4735.pin22, C1.1
  N11: SI4735.pin23, C8.1
  N12: SI4735.pin24, C7.1
  N13: L1.pin_0, C3.2
  N14: C2.1, FM_Antenna.antenna_lead
  N15: X1.1, R3.Pin_0, C5.2
  N16: TO_AMP.Ring, C8.2
  N17: TO_AMP.Tip, C7.2

notes:
  SI4735 - Minimal Schematic
  Ricardo Lima Caratti - Nov 2019
  SLC
  SDA
  RESET (RST)
  INTERRUPT
  Left Out
  Right Out
