# Fritzing sketch basic_schematic_with_buttons_internal_pullup_i2c (saved by Fritzing 0.9.3b)
circuit board: 11.6699cm x 8.25676cm
breadboards: 1

parts:
  part = Arduino Pro Mini v13
  L1 = Inductor [package="400 mil [THT]"]
  C3 = Capacitor [part_number=470nF package=cap-pth-large]
  C2 = Capacitor [part_number=1nF package=cap-pth-small2]
  FM_Antenna = Antenna
  C1 = Capacitor [part_number=22nF package=cap-pth-large]
  X1 = CRYSTAL [package=crystal-32khz-smd_epson_mc146]
  R3 = Resistor [tolerance=±5% resistance=2.2k package="0402 [SMD]"]
  R4 = Resistor [tolerance=±5% resistance=4.7k package="0402 [SMD]"]
  R5 = Resistor [tolerance=±5% resistance=4.7k package="0402 [SMD]"]
  C4 = Capacitor [part_number=100nF package=cap-pth-large]
  TO_AMP = Audio Jack (TRS) 3.5mm [package="4Ucon 08780 [THT]"]
  C7 = Capacitor [part_number=4.7uF package=cap-pth-large]
  C8 = Capacitor [part_number=4.7uF package=cap-pth-large]
  C5 = Capacitor [part_number=22pF package=cap-pth-large]
  C6 = Capacitor [part_number=22pF package=cap-pth-large]
  Encoder = Rotary Encoder [package=THT]
  S1 = SWITCH-MOMENTARY-2 [package=tactile-pth-12mm]
  S2 = SWITCH-MOMENTARY-2 [package=tactile-pth-12mm]
  S3 = SWITCH-MOMENTARY-2 [package=tactile-pth-12mm]
  S4 = SWITCH-MOMENTARY-2 [package=tactile-pth-12mm]
  S5 = SWITCH-MOMENTARY-2 [package=tactile-pth-12mm]
  S6 = SWITCH-MOMENTARY-2 [package=tactile-pth]
  S7 = SWITCH-MOMENTARY-2 [package=tactile-pth]
  S8 = SWITCH-MOMENTARY-2 [package=tactile-pth]
  S9 = SWITCH-MOMENTARY-2 [package=tactile_switch_smd]
  I2C_Device = Grove OLED 128x96
  1 = SSOP24 [chip_label=SI4735-D60 package=SSOP]

nets:
  3.3V: part.VCC, R4.Pin_0, R5.Pin_1, C4.2, 1.20, 1.21
  GND: part.GND, L1.pin_1, C4.1, C5.1, C6.1, Encoder.EncoderPinC, S3.1, I2C_Device.GND, 1.9, 1.10, 1.11, 1.13, 1.14, 1.16
  N1: part.A4, R4.Pin_1, I2C_Device.SDA, 1.18
  N2: part.A5, R5.Pin_0, I2C_Device.SCL
  N3: part.D13/SCK, S9.2
  N4: part.D12/MISO, 1.15
  N5: part.D11_PWM/MOSI, S8.2
  N6: part.D10_PWM/SS, S7.2
  N7: part.D9_PWM, S6.2
  N8: part.D8, S5.2
  N9: part.D7, S4.2
  N10: part.D6_PWM, S3.2
  N11: part.D5_PWM, S2.2
  N12: part.D4, S1.2
  N13: part.D3_PWM, Encoder.EncoderPinB
  N14: part.D2, Encoder.EncoderPinA
  N15: L1.pin_0, C3.2
  N16: C3.1, 1.12
  N17: C2.1, FM_Antenna.antenna_lead
  N18: C2.2, 1.8
  N19: C1.1, 1.22
  N20: X1.2, C6.2, 1.19
  N21: X1.1, R3.Pin_0, C5.2
  N22: R3.Pin_1, 1.3
  N23: TO_AMP.Ring, C8.2
  N24: TO_AMP.Tip, C7.2
  N25: C7.1, 1.24
  N26: C8.1, 1.23
  N27: S1.1, S4.1
  N28: S8.1, S9.1
  0V: I2C_Device.VCC

notes:
  SI4735 with I2C OLED or I2C LCD 20x4
  This circuit uses Arduino internal pullup resource
  Ricardo Lima Caratti - Dec 2019
  SCLK / SCL
  SDIO / SDA
  RESET (RST)
  Left Out
  Right Out
  SCL
  SDA
  Look for the right display Arduino Library to control your I2C device.
  Plese, check the right voltage of your I2C device.
  3.3V or 5V
  BFO
  AVC
  BANDWIDTH
  Volume Up
  Volume Down
  Band Up
  Band Down
  AGC
  STEP
  I2C buss address 0x11
  If you are using an Arduino Board based on ATmega328, pay attention on pin 13. It may not be the best option if your board has a LED circuit connected to this pin. In this case, use the digital pin 14 (A0) instead.
